// Logisim project cours01.circ as structural Verilog: 3 circuits, main circuit main
module main (
  input  [2:0] in_1,
  input  [2:0] in_2,
  input  in_3,
  input  in_4,
  input  in_5,
  output out_6,
  output out_7
);

  wire adder3bits_1_out_4, and_1_out, and_2_out, and_3_out;

  adder3bits adder3bits_1 (.out_4(adder3bits_1_out_4));  // open: in_1, in_2, in_3, out_5
  xor xor_1 (out_6, in_3, in_4, in_5);
  and and_1 (and_1_out, ~in_3, in_5);  // AND_Gate
  and and_2 (and_2_out, ~in_3, in_4);  // AND_Gate
  and and_3 (and_3_out, in_5, in_5);
  or or_1 (out_7, and_1_out, and_2_out, and_3_out);
endmodule

module adder2bits (
  input  in_1,
  input  in_2,
  output [1:0] out_3
);

  xor xor_1 (out_3[0], in_1, in_2);
  and and_1 (out_3[1], in_1, in_2);

  // Notes on the sheet:
  //   cheating
endmodule

module adder3bits (
  input  in_1,
  input  in_2,
  input  in_3,
  output out_4,
  output out_5
);

  wire and_1_out, and_2_out, and_3_out;

  xor xor_1 (out_4, in_1, in_3, in_2);
  and and_1 (and_1_out, in_1, in_2);
  and and_2 (and_2_out, in_1, in_3);
  and and_3 (and_3_out, in_2, in_3);
  or or_1 (out_5, and_1_out, and_2_out, and_3_out);
endmodule
