// Logisim project first_test.circ as structural Verilog: 1 circuit, main circuit main
module main (
);

  wire and_1_out, not_1_out, or_1_out;

  not not_1 (not_1_out, 1'b1);
  and and_1 (and_1_out, 1'b1, 1'b1);
  or or_1 (or_1_out, not_1_out, and_1_out);
  LED led_1 (.in(or_1_out));
endmodule
