// Logisim project serie01.circ as structural Verilog: 1 circuit, main circuit main
module main (
  input  in_1,
  input  in_2,
  input  in_3
);

  wire and_1_out, and_2_out, and_3_out, not_1_out, not_2_out, or_1_out, or_2_out, xor_1_out, xor_2_out,
       xor_3_out;

  not not_1 (not_1_out, in_2);
  not not_2 (not_2_out, in_3);
  xor xor_1 (xor_1_out, in_1, not_1_out);
  xor xor_2 (xor_2_out, not_1_out, not_2_out);
  and and_1 (and_1_out, in_3, xor_1_out);
  xor xor_3 (xor_3_out, not_2_out, in_1);
  or or_1 (or_1_out, and_1_out, and_2_out);
  and and_2 (and_2_out, in_1, xor_2_out);
  and and_3 (and_3_out, xor_3_out, in_2);
  or or_2 (or_2_out, or_1_out, and_3_out);
  LED led_1 (.in(or_2_out));
endmodule
