// Logisim project serie03.circ as structural Verilog: 1 circuit, main circuit main
module main (
  input  in_1,
  input  W,
  input  X,
  input  Y,
  input  Z
);

  wire a_out, and_1_out, and_2_out, and_3_out, and_4_out, and_5_out, and_6_out, and_7_out, and_8_out,
       and_9_out, and_10_out, and_11_out, and_12_out, and_13_out, and_14_out, and_15_out, and_16_out,
       and_17_out, and_18_out, and_19_out, and_20_out, and_21_out, and_22_out, and_23_out, and_24_out,
       and_25_out, and_26_out, b_out, c_out, d_out, e_out, f_out, g_out, not_1_out, not_2_out, not_3_out,
       not_4_out, not_5_out, not_6_out, not_7_out, not_8_out;

  not not_1 (not_1_out, W);
  not not_2 (not_2_out, X);
  not not_3 (not_3_out, Y);
  not not_4 (not_4_out, Z);
  not not_5 (not_5_out, not_1_out);
  not not_6 (not_6_out, not_2_out);
  not not_7 (not_7_out, not_3_out);
  not not_8 (not_8_out, not_4_out);
  and and_1 (and_1_out, not_5_out, not_2_out, not_3_out);
  and and_2 (and_2_out, not_1_out, not_6_out, not_8_out);
  and and_3 (and_3_out, not_1_out, not_2_out, not_4_out);
  and and_4 (and_4_out, not_1_out, not_7_out);
  and and_5 (and_5_out, not_1_out, not_2_out);
  and and_6 (and_6_out, not_1_out, not_7_out, not_8_out);
  and and_7 (and_7_out, not_1_out, not_3_out, not_4_out);
  and and_8 (and_8_out, not_2_out, not_3_out);
  and and_9 (and_9_out, not_1_out, not_6_out);
  and and_10 (and_10_out, not_1_out, not_8_out);
  and and_11 (and_11_out, not_2_out, not_3_out);
  and and_12 (and_12_out, not_5_out, not_2_out, not_3_out);
  and and_13 (and_13_out, not_1_out, not_6_out, not_3_out, not_8_out);
  and and_14 (and_14_out, not_1_out, not_2_out, not_7_out);
  and and_15 (and_15_out, not_1_out, not_2_out, not_4_out);
  and and_16 (and_16_out, not_1_out, not_7_out, not_4_out);
  and and_17 (and_17_out, not_1_out, not_7_out, not_4_out);
  and and_18 (and_18_out, not_2_out, not_3_out, not_4_out);
  and and_19 (and_19_out, not_5_out, not_2_out, not_3_out);
  and and_20 (and_20_out, not_1_out, not_6_out, not_3_out);
  and and_21 (and_21_out, not_1_out, not_6_out, not_4_out);
  and and_22 (and_22_out, not_1_out, not_3_out, not_4_out);
  and and_23 (and_23_out, not_5_out, not_2_out, not_3_out);
  and and_24 (and_24_out, not_1_out, not_6_out, not_3_out);
  and and_25 (and_25_out, not_1_out, not_6_out, not_4_out);
  and and_26 (and_26_out, not_1_out, not_2_out, not_7_out);
  or a (a_out, and_1_out, and_2_out, and_3_out, and_4_out);
  or b (b_out, and_5_out, and_6_out, and_7_out, and_8_out);
  or c (c_out, and_9_out, and_10_out, and_11_out);
  or d (d_out, and_12_out, and_13_out, and_14_out, and_15_out, and_16_out);
  or e (e_out, and_17_out, and_18_out);
  or f (f_out, and_19_out, and_20_out, and_21_out, and_22_out);
  or g (g_out, and_23_out, and_24_out, and_25_out, and_26_out);
  _7_Segment_Display u_7_segment_display_1 (
    .g(g_out), .f(f_out), .a(a_out), .b(b_out), .e(e_out), .d(d_out), .c(c_out));  // open: dp
endmodule
